# Fritzing sketch Garduino (saved by Fritzing 0.9.2b)
breadboards: 1

parts:
  Componente1 = Arduino Uno (Rev3)
  U1 = 7-SEGMENT-4DIGIT [package=7-segment-4digit-youngsun]
  DS1 = DS18B20 1-Wire Temperature Sensor [part_number=DS18B20]
  U2 = 2-Channel 5v Relay Shield [package=relay-2ch5v10a]

nets:
  N1: Componente1.A0, U2.IN2
  N2: Componente1.A1, U2.IN1
  N3: Componente1.D8, U1.13
  N4: Componente1.D10_PWM/SS, U1.11
  N5: Componente1.D13/SCK, DS1.DQ
  N6: Componente1.D0/RX, U1.1
  N7: Componente1.D1/TX, U1.2
  N8: Componente1.D2, U1.4
  N9: Componente1.D3_PWM, U1.5
  N10: Componente1.D4, U1.6
  N11: Componente1.D5_PWM, U1.16
  N12: Componente1.D6_PWM, U1.15
  N13: Componente1.D7, U1.14
  5V: Componente1.5V, DS1.VDD, U2.VCC
  GND: Componente1.GND, DS1.GND, U2.GND

custom parts:
  2-Channel 5v Relay Shield: 2 Channel 5v Relay Shield w. 2x SPD-06VDC-SD-C
